# Fritzing sketch fritzing (saved by Fritzing 0.9.6b)
breadboards: 1

parts:
  Mod1 = Raspberry Pi 4B
  PWM1 = PCA9685 16x12-bit PWM Breakout
  R1 = Resistor [tolerance=±5% resistance=220 package="0603 [SMD]"]
  R2 = Resistor [tolerance=±5% resistance=220 package="0603 [SMD]"]
  R3 = Resistor [tolerance=±5% resistance=220 package="0603 [SMD]"]
  R4 = Resistor [tolerance=±5% resistance=220 package="0603 [SMD]"]
  R5 = Resistor [tolerance=±5% resistance=220 package="0603 [SMD]"]
  R6 = Resistor [tolerance=±5% resistance=220 package="0603 [SMD]"]
  R7 = Resistor [tolerance=±5% resistance=220 package="0603 [SMD]"]
  R8 = Resistor [tolerance=±5% resistance=220 package="0603 [SMD]"]
  R9 = Resistor [tolerance=±5% resistance=220 package="0603 [SMD]"]
  R10 = Resistor [tolerance=±5% resistance=220 package="0603 [SMD]"]
  R11 = Resistor [tolerance=±5% resistance=220 package="0603 [SMD]"]
  R12 = Resistor [tolerance=±5% resistance=220 package="0603 [SMD]"]
  R13 = Resistor [tolerance=±5% resistance=220 package="0603 [SMD]"]
  R14 = Resistor [tolerance=±5% resistance=220 package="0603 [SMD]"]
  R15 = Resistor [tolerance=±5% resistance=220 package="0603 [SMD]"]
  LED16 = smd LED [color="Red (633nm)" current=0.030 package="1206 [SMD]"]
  LED17 = smd LED [color="Red (633nm)" current=0.030 package="1206 [SMD]"]
  LED18 = smd LED [color="Red (633nm)" current=0.030 package="1206 [SMD]"]
  LED19 = smd LED [color="Red (633nm)" current=0.030 package="1206 [SMD]"]
  LED20 = smd LED [color="Red (633nm)" current=0.030 package="1206 [SMD]"]
  LED21 = smd LED [color="Blue (430nm)" current=0.030 package="1206 [SMD]"]
  LED22 = smd LED [color="Blue (430nm)" current=0.030 package="1206 [SMD]"]
  LED23 = smd LED [color="Blue (430nm)" current=0.030 package="1206 [SMD]"]
  LED24 = smd LED [color="Blue (430nm)" current=0.030 package="1206 [SMD]"]
  LED25 = smd LED [color="Blue (430nm)" current=0.030 package="1206 [SMD]"]
  LED26 = smd LED [color="Yellow (574nm)" current=0.030 package="1206 [SMD]"]
  LED27 = smd LED [color="Yellow (574nm)" current=0.030 package="1206 [SMD]"]
  LED28 = smd LED [color="Yellow (574nm)" current=0.030 package="1206 [SMD]"]
  LED29 = smd LED [color="Yellow (574nm)" current=0.030 package="1206 [SMD]"]
  LED30 = smd LED [color="Yellow (574nm)" current=0.030 package="1206 [SMD]"]

nets:
  N1: Mod1.5V, PWM1.no_name_yet#506
  N2: Mod1.GPIO2, PWM1.no_name_yet#504
  N3: Mod1.GPIO3, PWM1.no_name_yet#503
  N4: Mod1.GND, PWM1.no_name_yet#501, PWM1.no_name_yet#1000, PWM1.no_name_yet#1001, PWM1.no_name_yet#1002, PWM1.no_name_yet#1003, PWM1.no_name_yet#1004, PWM1.no_name_yet#1005, PWM1.no_name_yet#1006, PWM1.no_name_yet#1007, PWM1.no_name_yet#1008, PWM1.no_name_yet#1009, PWM1.no_name_yet#1010, PWM1.no_name_yet#1011, PWM1.no_name_yet#1012, PWM1.no_name_yet#1013, PWM1.no_name_yet#1014, LED16.anode, LED17.anode, LED18.anode, LED19.anode, LED20.anode, LED21.anode, LED22.anode, LED23.anode, LED24.anode, LED25.anode, LED26.anode, LED27.anode, LED28.anode, LED29.anode, LED30.anode
  N5: PWM1.no_name_yet#0, R1.Pin_1
  N6: PWM1.no_name_yet#1, R2.Pin_1
  N7: PWM1.no_name_yet#2, R3.Pin_1
  N8: PWM1.no_name_yet#3, R4.Pin_1
  N9: PWM1.no_name_yet#4, R5.Pin_1
  N10: PWM1.no_name_yet#5, R9.Pin_1
  N11: PWM1.no_name_yet#6, R8.Pin_1
  N12: PWM1.no_name_yet#7, R10.Pin_1
  N13: PWM1.no_name_yet#8, R6.Pin_1
  N14: PWM1.no_name_yet#9, R7.Pin_1
  N15: PWM1.no_name_yet#10, R14.Pin_1
  N16: PWM1.no_name_yet#11, R13.Pin_1
  N17: PWM1.no_name_yet#12, R15.Pin_1
  N18: PWM1.no_name_yet#13, R11.Pin_1
  N19: PWM1.no_name_yet#14, R12.Pin_1
  N20: R1.Pin_0, LED16.cathode
  N21: R2.Pin_0, LED17.cathode
  N22: R3.Pin_0, LED18.cathode
  N23: R4.Pin_0, LED19.cathode
  N24: R5.Pin_0, LED20.cathode
  N25: R6.Pin_0, LED24.cathode
  N26: R7.Pin_0, LED22.cathode
  N27: R8.Pin_0, LED21.cathode
  N28: R9.Pin_0, LED25.cathode
  N29: R10.Pin_0, LED23.cathode
  N30: R11.Pin_0, LED29.cathode
  N31: R12.Pin_0, LED27.cathode
  N32: R13.Pin_0, LED26.cathode
  N33: R14.Pin_0, LED30.cathode
  N34: R15.Pin_0, LED28.cathode
